// Digital circuit CPU.dig as structural Verilog
module CPU (
  input  clk
);

  wire comparator_1_eq, comparator_2_eq, comparator_3_eq, comparator_4_eq;
  wire [7:0] programme_counter_1_p1, rom_1_d;
  wire [15:0] programme_counter_1_p2, programme_counter_1_p6;

  Comparator #(.Bits(8)) comparator_1 (.a(rom_1_d), .b(8'h1), .eq(comparator_1_eq));  // open: gt, lt
  Comparator #(.Bits(8)) comparator_2 (.a(rom_1_d), .b(8'h1), .eq(comparator_2_eq));  // open: gt, lt
  // Programme_Counter programme_counter_1: pin names not known; wires that end beside it: programme_counter_1_p1, programme_counter_1_p2, clk, comparator_1_eq, comparator_2_eq, programme_counter_1_p6
  ALU alu_1 (.CMD(rom_1_d), .DAT(programme_counter_1_p1), .CLK(clk), .Q(programme_counter_1_p1));
  Comparator #(.Bits(8)) comparator_3 (.a(rom_1_d), .b(8'h1), .eq(comparator_3_eq));  // open: gt, lt
  Comparator #(.Bits(8)) comparator_4 (.a(rom_1_d), .b(8'h1), .eq(comparator_4_eq));  // open: gt, lt
  ROM #(.AddrBits(16), .Bits(8)) rom_1 (.A(programme_counter_1_p6), .sel(1'b1), .D(rom_1_d));
  ROM #(.AddrBits(16), .Bits(8)) rom_2 (.A(programme_counter_1_p6), .sel(1'b1), .D(programme_counter_1_p1));
  ROM #(.AddrBits(16), .Bits(16)) rom_3 (.A(programme_counter_1_p6), .sel(1'b1), .D(programme_counter_1_p2));
  RAMDualPort #(.AddrBits(16), .Bits(8)) ramdualport_1 (
    .A(programme_counter_1_p2), .Din(programme_counter_1_p1), .str(comparator_3_eq), .C(clk),
    .ld(comparator_4_eq), .D(programme_counter_1_p1));

  // Notes on the sheet:
  //   clk: Hz: 10
  //   LN: output from the programmme counter,
  //   the current line of code being executed
  //   LN
  //   CMD
  //   DAT
  //   ADR
  //   CLK
endmodule
